// Logisim project cpu.circ as structural Verilog: 5 circuits, main circuit main
module main (
);

  wire and_1_out, and_2_out, and_3_out, and_4_out, and_6_out, and_7_out, and_8_out, and_9_out,
       bit_extender_1_out, bitselector_1_out, bitselector_2_out, bitselector_3_out, bitselector_6_out,
       bitselector_7_out, bitselector_8_out, bitselector_9_out, bitselector_11_out, bitselector_12_out,
       bitselector_13_out, d_ff_1_q, d_ff_2_q, d_ff_3_q, d_ff_4_q, DECODE_SUBCYCLE_carry, EXEC_MEMACC,
       FallingPulseGen_1_pulse, multiplexer_10_out, multiplexer_13_out, nor_1_out, nor_2_out, nor_3_out,
       or_1_out, or_2_out, or_3_out, or_4_out, R_WE, xnor_1_out, xnor_2_out, xnor_3_out, xnor_4_out,
       xnor_5_out, xnor_6_out, xnor_7_out, xnor_8_out, xnor_9_out, xnor_10_out, xnor_11_out, xnor_12_out;
  wire [2:0] FETCH_SUBCYCLE_q;
  wire [3:0] bitselector_14_out, DECODE_SUBCYCLE_q, instr_size_out, multiplexer_6_out, N_OPERATIONS,
       OP_SUBCYCLE_q, OPERATION_SEL, PLA_1_out;
  wire [7:0] bitselector_4_out, bitselector_5_out, bitselector_10_out, multiplexer_1_out, multiplexer_3_out,
       multiplexer_9_out, multiplexer_12_out, R_READ_SEL, R_WRITE_SEL, ROM_1_p2, ROM_1_p3, undriven,
       undriven_2;
  wire [11:0] ROM_1_p1;
  wire [13:0] OPERATION, ROM_2_data;
  wire [14:0] PC_q;
  wire [15:0] ADDR_BUS, CRT_INST, CTL_BUS, DATA_BUS, DATA_IN, MAR_q, MDR_q, MEM_ADDR, multiplexer_2_out,
       multiplexer_4_out, multiplexer_5_out, multiplexer_7_out, multiplexer_8_out, multiplexer_11_out,
       R_DATA_IN, R_DATA_OUT, register_2_q;

  BitSelector #(.width(16)) bitselector_1 (.in(CTL_BUS), .out(bitselector_1_out), .sel(4'b0011));
  BitSelector #(.width(16)) bitselector_2 (.in(CTL_BUS), .out(bitselector_2_out), .sel(4'b0100));
  Multiplexer #(.width(8)) multiplexer_1 (.in0(8'h20), .in1(8'h29), .out(multiplexer_1_out), .sel(bitselector_3_out));
  BitSelector #(.width(16)) bitselector_3 (.in(CRT_INST), .out(bitselector_3_out), .sel(4'b1000));
  BitSelector #(.group(8), .width(16)) bitselector_4 (.in(CRT_INST), .out(bitselector_4_out), .sel(1'b0));
  BitSelector #(.group(8), .width(16)) bitselector_5 (.in(CRT_INST), .out(bitselector_5_out), .sel(1'b1));
  BitSelector #(.width(16)) bitselector_6 (.in(CRT_INST), .out(bitselector_6_out), .sel(4'b0111));
  BitSelector #(.width(16)) bitselector_7 (.in(CTL_BUS), .out(bitselector_7_out), .sel(4'b0000));
  and and_1 (and_1_out, bitselector_1_out, ~bitselector_2_out);  // AND_Gate
  Multiplexer #(.width(16)) multiplexer_2 (
    .in0({{8{1'b0}}, bitselector_5_out}), .in1({bitselector_5_out, {8{1'b0}}}), .out(multiplexer_2_out),
    .sel(bitselector_6_out));
  nor nor_1 (nor_1_out, FETCH_SUBCYCLE_q[2], FETCH_SUBCYCLE_q[1], FETCH_SUBCYCLE_q[0]);
  Multiplexer #(.select(4), .width(8)) multiplexer_3 (
    .in0(multiplexer_1_out), .in1(8'h21), .out(multiplexer_3_out), .sel(DECODE_SUBCYCLE_q));  // open: in2, in3, in4, in5, in6, in7, in8, in9, in10, in11, in12, in13, in14, in15
  or or_1 (or_1_out, ~bitselector_3_out, nor_2_out);  // OR_Gate
  Multiplexer #(.width(16)) multiplexer_4 (
    .in1(multiplexer_2_out), .out(multiplexer_4_out), .sel(bitselector_3_out));  // open: in0
  nor nor_2 (nor_2_out, DECODE_SUBCYCLE_q[3], DECODE_SUBCYCLE_q[2], DECODE_SUBCYCLE_q[1], DECODE_SUBCYCLE_q[0]);
  Multiplexer #(.select(4), .width(16)) multiplexer_5 (
    .in0(multiplexer_4_out), .out(multiplexer_5_out), .sel(DECODE_SUBCYCLE_q));  // open: in1, in2, in3, in4, in5, in6, in7, in8, in9, in10, in11, in12, in13, in14, in15
  Bit_Extender #(.in_width(16), .out_width(1)) bit_extender_1 (.in(CTL_BUS), .out(bit_extender_1_out));
  BitSelector #(.width(16)) bitselector_8 (.in(CTL_BUS), .out(bitselector_8_out), .sel(4'b0011));
  BitSelector #(.width(16)) bitselector_9 (.in(CTL_BUS), .out(bitselector_9_out), .sel(4'b0100));
  buf or_2 (or_2_out, nor_1_out);  // OR_Gate
  assign R_WRITE_SEL = and_1_out ? multiplexer_3_out : 8'bz;  // Controlled_Buffer controlled_buffer_1
  assign R_WE = and_1_out ? or_1_out : 1'bz;  // Controlled_Buffer controlled_buffer_2
  assign R_DATA_IN = and_1_out ? multiplexer_5_out : 16'bz;  // Controlled_Buffer controlled_buffer_3
  PLA #(.in_width(8), .out_width(4), .\table ("11000001 0010\n11000010 0010")) instr_size (
    .in(bitselector_4_out), .out(instr_size_out));
  and and_2 (and_2_out, nor_3_out, or_2_out);
  nor nor_3 (nor_3_out, bitselector_8_out, bitselector_9_out);
  ROM #(.addrWidth(12), .dataWidth(14)) ROM_2 (.addr({bitselector_4_out, DECODE_SUBCYCLE_q}), .data(ROM_2_data));
  Counter #(.max('h7fff), .width(15)) PC (
    .clr(1'b0), .load(1'b0), .up(1'b1), .count(and_2_out), .clk(bit_extender_1_out), .D(DATA_BUS[15:1]),
    .Q(PC_q));  // open: carry
  Counter #(.max('h2), .width(3)) FETCH_SUBCYCLE (
    .clr(1'b0), .load(1'b0), .up(1'b1), .count(nor_3_out), .clk(bit_extender_1_out), .carry(CTL_BUS[6]),
    .Q(FETCH_SUBCYCLE_q));  // open: D
  Register #(.width(16)) INSTR_REGISTER (
    .D(DATA_BUS), .en(FETCH_SUBCYCLE_q[1]), .clk(bit_extender_1_out), .Q(CRT_INST));  // open: clr
  and and_3 (and_3_out, and_1_out, and_4_out);
  D_Flip_Flop d_ff_1 (.D(and_3_out), .clk(bitselector_7_out), .Q(d_ff_1_q));  // open: Qn, preset, reset
  Counter #(.max('hf), .width(4)) DECODE_SUBCYCLE (
    .clr(d_ff_1_q), .load(1'b0), .up(1'b1), .count(and_1_out), .clk(bitselector_7_out),
    .carry(DECODE_SUBCYCLE_carry), .Q(DECODE_SUBCYCLE_q));  // open: D
  assign ADDR_BUS = nor_3_out ? {PC_q, 1'b0} : 16'bz;  // Controlled_Buffer controlled_buffer_4
  assign CTL_BUS[1] = nor_3_out ? 1'b1 : 1'bz;  // Controlled_Buffer controlled_buffer_5
  and and_4 (and_4_out, xnor_1_out, xnor_2_out, xnor_3_out, xnor_4_out);
  xnor xnor_1 (xnor_1_out, instr_size_out[0], DECODE_SUBCYCLE_q[0]);
  xnor xnor_2 (xnor_2_out, DECODE_SUBCYCLE_q[1], instr_size_out[1]);
  xnor xnor_3 (xnor_3_out, instr_size_out[2], DECODE_SUBCYCLE_q[2]);
  xnor xnor_4 (xnor_4_out, instr_size_out[3], DECODE_SUBCYCLE_q[3]);
  and and_5 (CTL_BUS[7], and_3_out, and_1_out);
  RAM #(.addrWidth(4), .dataWidth(14)) RAM_2 (
    .addr(multiplexer_6_out), .we(and_1_out), .oe(1'b1), .clk(bitselector_7_out), .din(ROM_2_data),
    .dout(OPERATION));
  Multiplexer #(.width(4)) multiplexer_6 (
    .in0(OPERATION_SEL), .in1(DECODE_SUBCYCLE_q), .out(multiplexer_6_out), .sel(and_1_out));
  assign CTL_BUS[1] = and_1_out ? 1'b0 : 1'bz;  // Controlled_Buffer controlled_buffer_6
  assign CTL_BUS[2] = and_1_out ? 1'b0 : 1'bz;  // Controlled_Buffer controlled_buffer_7
  Register #(.width(4)) register_1 (
    .D(instr_size_out), .en(and_1_out), .clk(bitselector_7_out), .Q(N_OPERATIONS));  // open: clr
  Clock clock_1 (.out(CTL_BUS[0]));
  or or_3 (or_3_out, CTL_BUS[6], CTL_BUS[7], CTL_BUS[8]);
  BitSelector #(.group(8), .width(10)) bitselector_10 (.in(OPERATION[13:4]), .out(bitselector_10_out), .sel(1'b0));
  D_Flip_Flop d_ff_2 (.D(CTL_BUS[5]), .clk(CTL_BUS[0]), .Q(d_ff_2_q));  // open: Qn, preset, reset
  Counter #(.max('h3), .width(2)) CYCLE_STAGE (
    .clr(d_ff_2_q), .load(1'b0), .up(1'b1), .count(or_3_out), .clk(CTL_BUS[0]), .carry(CTL_BUS[5]),
    .Q(CTL_BUS[4:3]));  // open: D
  BitSelector #(.width(16)) bitselector_11 (.in(CTL_BUS), .out(bitselector_11_out), .sel(4'b0000));
  BitSelector #(.width(16)) bitselector_12 (.in(CTL_BUS), .out(bitselector_12_out), .sel(4'b0011));
  BitSelector #(.width(16)) bitselector_13 (.in(CTL_BUS), .out(bitselector_13_out), .sel(4'b0100));
  and and_6 (and_6_out, ~bitselector_12_out, bitselector_13_out);  // AND_Gate
  BitSelector #(.group(4), .width(14)) bitselector_14 (.in(OPERATION), .out(bitselector_14_out), .sel(2'b00));
  Multiplexer #(.select(4), .width(16)) multiplexer_7 (
    .in1({16{1'b0}}), .in2(R_DATA_OUT), .out(multiplexer_7_out), .sel(bitselector_14_out));  // open: in0, in3, in4, in5, in6, in7, in8, in9, in10, in11, in12, in13, in14, in15
  Multiplexer #(.select(4), .width(16)) multiplexer_8 (
    .in1({16{1'b0}}), .in2({16{1'b0}}), .out(multiplexer_8_out), .sel(bitselector_14_out));  // open: in0, in3, in4, in5, in6, in7, in8, in9, in10, in11, in12, in13, in14, in15
  Multiplexer #(.select(4), .width(8)) multiplexer_9 (
    .in1(bitselector_10_out), .in2({8{1'b0}}), .out(multiplexer_9_out), .sel(bitselector_14_out));  // open: in0, in3, in4, in5, in6, in7, in8, in9, in10, in11, in12, in13, in14, in15
  Multiplexer #(.select(4)) multiplexer_10 (
    .in0(1'b0), .in1(1'b0), .in2(1'b1), .out(multiplexer_10_out), .sel(bitselector_14_out));  // open: in3, in4, in5, in6, in7, in8, in9, in10, in11, in12, in13, in14, in15
  D_Flip_Flop d_ff_3 (.D(and_8_out), .clk(bitselector_11_out), .Q(d_ff_3_q));  // open: Qn, preset, reset
  PLA #(.in_width(4), .out_width(4), .\table ("0001 0001 # DB READ\n0010 0001 # DB WRITE\n0011 0010 # AB WRITE\n0100 0010 # MEM WRITE\n0000 0001 # EOI")) PLA_1 (
    .in(bitselector_14_out), .out(PLA_1_out));
  and and_7 (and_7_out, and_6_out, and_9_out);
  Multiplexer #(.select(4), .width(16)) multiplexer_11 (
    .in1(DATA_BUS), .in2({16{1'b0}}), .out(multiplexer_11_out), .sel(bitselector_14_out));  // open: in0, in3, in4, in5, in6, in7, in8, in9, in10, in11, in12, in13, in14, in15
  Multiplexer #(.select(4), .width(8)) multiplexer_12 (
    .in1({8{1'b0}}), .in2(bitselector_10_out), .out(multiplexer_12_out), .sel(bitselector_14_out));  // open: in0, in3, in4, in5, in6, in7, in8, in9, in10, in11, in12, in13, in14, in15
  Multiplexer #(.select(4)) multiplexer_13 (
    .in1(1'b1), .in2(1'b0), .out(multiplexer_13_out), .sel(bitselector_14_out));  // open: in0, in3, in4, in5, in6, in7, in8, in9, in10, in11, in12, in13, in14, in15
  Multiplexer #(.select(4)) multiplexer_14 (
    .in1(1'b0), .in2(1'b0), .out(EXEC_MEMACC), .sel(bitselector_14_out));  // open: in0, in3, in4, in5, in6, in7, in8, in9, in10, in11, in12, in13, in14, in15
  and and_8 (and_8_out, xnor_5_out, xnor_6_out, xnor_7_out, xnor_8_out);
  D_Flip_Flop d_ff_4 (.D(and_7_out), .clk(bitselector_11_out), .Q(d_ff_4_q));  // open: Qn, preset, reset
  and and_9 (and_9_out, xnor_9_out, xnor_10_out, xnor_11_out, xnor_12_out);
  xnor xnor_5 (xnor_5_out, N_OPERATIONS[0], OPERATION_SEL[0]);
  xnor xnor_6 (xnor_6_out, OPERATION_SEL[1], N_OPERATIONS[1]);
  xnor xnor_7 (xnor_7_out, N_OPERATIONS[2], OPERATION_SEL[2]);
  xnor xnor_8 (xnor_8_out, N_OPERATIONS[3], OPERATION_SEL[3]);
  Counter #(.max('hf), .width(4)) EXECUTE_SUBCYCLE (
    .clr(d_ff_3_q), .load(1'b0), .up(1'b1), .count(and_7_out), .clk(bitselector_11_out), .Q(OPERATION_SEL));  // open: D, carry
  Counter #(.max('hf), .width(4)) OP_SUBCYCLE (
    .clr(d_ff_4_q), .load(1'b0), .up(1'b1), .count(and_6_out), .clk(bitselector_11_out), .Q(OP_SUBCYCLE_q));  // open: D, carry
  xnor xnor_9 (xnor_9_out, PLA_1_out[0], OP_SUBCYCLE_q[0]);
  xnor xnor_10 (xnor_10_out, OP_SUBCYCLE_q[1], PLA_1_out[1]);
  xnor xnor_11 (xnor_11_out, PLA_1_out[2], OP_SUBCYCLE_q[2]);
  xnor xnor_12 (xnor_12_out, PLA_1_out[3], OP_SUBCYCLE_q[3]);
  FallingPulseGen FallingPulseGen_1 (
    .D(multiplexer_13_out), .CLOCK(bitselector_11_out), .PULSE(FallingPulseGen_1_pulse));
  assign ADDR_BUS = and_6_out ? multiplexer_8_out : 16'bz;  // Controlled_Buffer controlled_buffer_8
  assign R_WRITE_SEL = and_6_out ? multiplexer_9_out : 8'bz;  // Controlled_Buffer controlled_buffer_9
  assign R_DATA_IN = and_6_out ? multiplexer_11_out : 16'bz;  // Controlled_Buffer controlled_buffer_10
  assign R_READ_SEL = and_6_out ? multiplexer_12_out : 8'bz;  // Controlled_Buffer controlled_buffer_11
  assign R_WE = and_6_out ? FallingPulseGen_1_pulse : 1'bz;  // Controlled_Buffer controlled_buffer_12
  and and_10 (CTL_BUS[8], and_8_out, and_6_out);
  // AND_Gate and_11 is placed but not wired
  assign CTL_BUS[1] = and_6_out ? EXEC_MEMACC : 1'bz;  // Controlled_Buffer controlled_buffer_13
  Register #(.width(16)) register_2 (
    .D(multiplexer_7_out), .en(multiplexer_10_out), .clk(bitselector_11_out), .Q(register_2_q));  // open: clr
  assign DATA_BUS = and_6_out ? register_2_q : 16'bz;  // Controlled_Buffer controlled_buffer_14
  Register #(.width(16)) MDR (.D(DATA_IN), .en(1'b1), .clk(CTL_BUS[0]), .Q(MDR_q));  // open: clr
  Register #(.width(16)) MAR (.D(ADDR_BUS), .en(1'b1), .clk(CTL_BUS[0]), .Q(MAR_q));  // open: clr
  assign DATA_BUS = CTL_BUS[1] ? MDR_q : 16'bz;  // Controlled_Buffer controlled_buffer_15
  assign MEM_ADDR = CTL_BUS[1] ? MAR_q : 16'bz;  // Controlled_Buffer controlled_buffer_16
  MultiRegisterFile MultiRegisterFile_1 (
    .R_WE(R_WE), .R_WRITE_SEL(R_WRITE_SEL), .R_DATA_IN(R_DATA_IN), .R_READ_SEL(R_READ_SEL),
    .CTL_BUS(CTL_BUS), .R_DATA_OUT(R_DATA_OUT));
  or or_4 (or_4_out, MEM_ADDR[12], MEM_ADDR[13], MEM_ADDR[14], MEM_ADDR[15]);
  // ROM #(.addrWidth(12), .line("dual"), .misaligned("true")) ROM_1: pin names not known; wires that end beside it: ROM_1_p1, ROM_1_p2, ROM_1_p3
  Bit_Extender #(.in_width(16), .out_width(12)) bit_extender_2 (.in(MEM_ADDR), .out(ROM_1_p1));
  // RAM #(.addrWidth(16), .enables("line"), .line("dual"), .misaligned("true")) RAM_1: pin names not known; wires that end beside it: MEM_ADDR, CTL_BUS[2], 1'b1, 1'b1, CTL_BUS[0]
  Multiplexer #(.width(16)) multiplexer_15 (
    .in0({ROM_1_p3, ROM_1_p2}), .in1({undriven_2, undriven}), .out(DATA_IN), .sel(or_4_out));

  // Notes on the sheet:
  //   contents of ROM_2 (hex, n*v repeats v):
  //   3088*0 292 11 14*0 292 21
  //   contents of ROM_1 (hex, n*v repeats v):
  //   c1 ff c2 ff
endmodule

module RegisterFile (
  input  [3:0] R_READ_SEL,
  input  [3:0] R_WRITE_SEL,
  input  [15:0] DATA_IN,
  input  WE,
  input  CLOCK,
  output [15:0] DATA_OUT
);

  wire decoder_1_out0, decoder_1_out1, decoder_1_out2, decoder_1_out3, decoder_1_out4, decoder_1_out5,
       decoder_1_out6, decoder_1_out7, decoder_1_out8, decoder_1_out9, decoder_1_out10, decoder_1_out11,
       decoder_1_out12, decoder_1_out13, decoder_1_out14, decoder_1_out15;
  wire [15:0] register_1_q, register_2_q, register_3_q, register_4_q, register_5_q, register_6_q,
       register_7_q, register_8_q, register_9_q, register_10_q, register_11_q, register_12_q, register_13_q,
       register_14_q, register_15_q, register_16_q;

  Decoder #(.select(4)) decoder_1 (
    .out0(decoder_1_out0), .out1(decoder_1_out1), .out2(decoder_1_out2), .out3(decoder_1_out3),
    .out4(decoder_1_out4), .out5(decoder_1_out5), .out6(decoder_1_out6), .out7(decoder_1_out7),
    .out8(decoder_1_out8), .out9(decoder_1_out9), .out10(decoder_1_out10), .out11(decoder_1_out11),
    .out12(decoder_1_out12), .out13(decoder_1_out13), .out14(decoder_1_out14), .out15(decoder_1_out15),
    .sel(R_WRITE_SEL), .en(WE));
  Register #(.width(16)) register_1 (.D(DATA_IN), .en(decoder_1_out0), .clk(CLOCK), .Q(register_1_q));  // open: clr
  Register #(.width(16)) register_2 (.D(DATA_IN), .en(decoder_1_out1), .clk(CLOCK), .Q(register_2_q));  // open: clr
  Register #(.width(16)) register_3 (.D(DATA_IN), .en(decoder_1_out2), .clk(CLOCK), .Q(register_3_q));  // open: clr
  Register #(.width(16)) register_4 (.D(DATA_IN), .en(decoder_1_out3), .clk(CLOCK), .Q(register_4_q));  // open: clr
  Register #(.width(16)) register_5 (.D(DATA_IN), .en(decoder_1_out4), .clk(CLOCK), .Q(register_5_q));  // open: clr
  Register #(.width(16)) register_6 (.D(DATA_IN), .en(decoder_1_out5), .clk(CLOCK), .Q(register_6_q));  // open: clr
  Register #(.width(16)) register_7 (.D(DATA_IN), .en(decoder_1_out6), .clk(CLOCK), .Q(register_7_q));  // open: clr
  Register #(.width(16)) register_8 (.D(DATA_IN), .en(decoder_1_out7), .clk(CLOCK), .Q(register_8_q));  // open: clr
  Register #(.width(16)) register_9 (.D(DATA_IN), .en(decoder_1_out8), .clk(CLOCK), .Q(register_9_q));  // open: clr
  Register #(.width(16)) register_10 (.D(DATA_IN), .en(decoder_1_out9), .clk(CLOCK), .Q(register_10_q));  // open: clr
  Register #(.width(16)) register_11 (.D(DATA_IN), .en(decoder_1_out10), .clk(CLOCK), .Q(register_11_q));  // open: clr
  Register #(.width(16)) register_12 (.D(DATA_IN), .en(decoder_1_out11), .clk(CLOCK), .Q(register_12_q));  // open: clr
  Register #(.width(16)) register_13 (.D(DATA_IN), .en(decoder_1_out12), .clk(CLOCK), .Q(register_13_q));  // open: clr
  Register #(.width(16)) register_14 (.D(DATA_IN), .en(decoder_1_out13), .clk(CLOCK), .Q(register_14_q));  // open: clr
  Register #(.width(16)) register_15 (.D(DATA_IN), .en(decoder_1_out14), .clk(CLOCK), .Q(register_15_q));  // open: clr
  Register #(.width(16)) register_16 (.D(DATA_IN), .en(decoder_1_out15), .clk(CLOCK), .Q(register_16_q));  // open: clr
  Multiplexer #(.select(4), .width(16)) multiplexer_1 (
    .in0(register_1_q), .in1(register_2_q), .in2(register_3_q), .in3(register_4_q), .in4(register_5_q),
    .in5(register_6_q), .in6(register_7_q), .in7(register_8_q), .in8(register_9_q), .in9(register_10_q),
    .in10(register_11_q), .in11(register_12_q), .in12(register_13_q), .in13(register_14_q),
    .in14(register_15_q), .in15(register_16_q), .out(DATA_OUT), .sel(R_READ_SEL));
endmodule

module MultiRegisterFile (
  input  R_WE,
  input  [7:0] R_WRITE_SEL,
  input  [15:0] R_DATA_IN,
  input  [7:0] R_READ_SEL,
  input  [15:0] CTL_BUS,
  output [15:0] R_DATA_OUT
);

  wire bitselector_1_out, decoder_1_out0, decoder_1_out1, decoder_1_out2;
  wire [3:0] bitselector_2_out, bitselector_3_out, bitselector_4_out, bitselector_5_out;
  wire [15:0] GEN_REG_data_out, TMPREGS_data_out, UREGS_data_out;

  BitSelector #(.width(16)) bitselector_1 (.in(CTL_BUS), .out(bitselector_1_out), .sel(4'b0000));
  Decoder #(.select(4)) decoder_1 (
    .out0(decoder_1_out0), .out1(decoder_1_out1), .out2(decoder_1_out2), .sel(bitselector_2_out), .en(R_WE));  // open: out3, out4, out5, out6, out7, out8, out9, out10, out11, out12, out13, out14, out15
  BitSelector #(.group(4)) bitselector_2 (.in(R_WRITE_SEL), .out(bitselector_2_out), .sel(1'b1));
  BitSelector #(.group(4)) bitselector_3 (.in(R_WRITE_SEL), .out(bitselector_3_out), .sel(1'b0));
  BitSelector #(.group(4)) bitselector_4 (.in(R_READ_SEL), .out(bitselector_4_out), .sel(1'b0));
  RegisterFile GEN_REG (
    .R_READ_SEL(bitselector_4_out), .R_WRITE_SEL(bitselector_3_out), .DATA_IN(R_DATA_IN),
    .WE(decoder_1_out0), .CLOCK(bitselector_1_out), .DATA_OUT(GEN_REG_data_out));
  RegisterFile UREGS (
    .R_READ_SEL(bitselector_4_out), .R_WRITE_SEL(bitselector_3_out), .DATA_IN(R_DATA_IN),
    .WE(decoder_1_out2), .CLOCK(bitselector_1_out), .DATA_OUT(UREGS_data_out));
  RegisterFile TMPREGS (
    .R_READ_SEL(bitselector_4_out), .R_WRITE_SEL(bitselector_3_out), .DATA_IN(R_DATA_IN),
    .WE(decoder_1_out1), .CLOCK(bitselector_1_out), .DATA_OUT(TMPREGS_data_out));
  BitSelector #(.group(4)) bitselector_5 (.in(R_READ_SEL), .out(bitselector_5_out), .sel(1'b1));
  Multiplexer #(.select(4), .width(16)) multiplexer_1 (
    .in0(GEN_REG_data_out), .in1(TMPREGS_data_out), .in2(UREGS_data_out), .out(R_DATA_OUT),
    .sel(bitselector_5_out));  // open: in3, in4, in5, in6, in7, in8, in9, in10, in11, in12, in13, in14, in15

  // Notes on the sheet:
  //   R_DATA_OUT: pull=down
  //   R_WE: pull=down
  //   R_DATA_IN: pull=down
  //   R_READ_SEL: pull=down
  //   CTL_BUS: pull=down
  //   R_WRITE_SEL: pull=down
endmodule

module PulseGen (
  input  D,
  input  CLOCK,
  output PULSE
);

  wire d_ff_1_qn, d_ff_2_q;

  D_Flip_Flop d_ff_1 (.D(D), .clk(CLOCK), .Qn(d_ff_1_qn));  // open: Q, preset, reset
  D_Flip_Flop d_ff_2 (.D(d_ff_1_qn), .clk(CLOCK), .Q(d_ff_2_q));  // open: Qn, preset, reset
  and and_1 (PULSE, D, d_ff_2_q);
endmodule

module FallingPulseGen (
  input  D,
  input  CLOCK,
  output PULSE
);

  wire d_ff_1_qn, d_ff_2_q;

  D_Flip_Flop #(.trigger("falling")) d_ff_1 (.D(D), .clk(CLOCK), .Qn(d_ff_1_qn));  // open: Q, preset, reset
  D_Flip_Flop #(.trigger("falling")) d_ff_2 (.D(d_ff_1_qn), .clk(CLOCK), .Q(d_ff_2_q));  // open: Qn, preset, reset
  and and_1 (PULSE, D, d_ff_2_q);
endmodule
